# Fritzing sketch breadboard (saved by Fritzing 0.9.3b)
breadboards: 1

parts:
  Part1 = Arduino Nano (Rev3.0)
  S2 = Momentary Switch [part_number=b package=ksa_sealed_tac_switch]
  S3 = Momentary Switch [part_number=a package=ksa_sealed_tac_switch]
  S4 = Momentary Switch [part_number=left package=ksa_sealed_tac_switch]
  S5 = Momentary Switch [part_number=right package=ksa_sealed_tac_switch]
  S6 = Momentary Switch [part_number=up package=ksa_sealed_tac_switch]
  J1 = Piezo Speaker
  Squix1 = OLED 0.96" 128x64 I2C SSD1306
  R2 = Resistor [tolerance=±5% resistance=220 package=THT]
  R3 = Resistor [tolerance=±5% resistance=220 package=THT]
  LED1 = LED - 3mm [color="Red (633nm)" package="3 mm [THT]"]
  LED3 = LED - 3mm [color="Yellow (595nm)" package="3 mm [THT]"]
  LED4 = LED - 3mm [color="Green (555nm)" package="3 mm [THT]"]
  S1 = Momentary Switch [part_number=down package=ksa_sealed_tac_switch]
  R4 = Resistor [tolerance=±1% resistance=10k package=THT]
  R1 = Resistor [tolerance=±5% resistance=220 package=THT]

nets:
  GND: Part1.GND, S2.1, S2.2, S3.1, S3.2, S4.1, S5.1, S6.1, S6.2, Squix1.GND, LED1.cathode, LED3.cathode, LED4.cathode, S1.1, S1.2
  N1: Part1.D2, S1.3, S1.4
  N2: Part1.D3, S5.3
  N3: Part1.D4, S3.3, S3.4
  N4: Part1.D5, R3.Pin_1
  N5: Part1.D6, R2.Pin_1
  N6: Part1.D7, R1.Pin_1
  N7: Part1.D9, R4.Pin_1
  N8: Part1.D11/MOSI, J1.pin1
  5V: Part1.5V, Squix1.VCC
  N9: Part1.A5, Squix1.SCL
  N10: Part1.A4, Squix1.SCA
  N11: Part1.A3, S6.3, S6.4
  N12: Part1.A2, S2.3, S2.4
  N13: Part1.A1, S4.3
  N14: J1.pin2, R4.Pin_0
  N15: R2.Pin_0, LED3.anode
  N16: R3.Pin_0, LED1.anode
  N17: LED4.anode, R1.Pin_0
